# Fritzing sketch ultrasonic_lcd (saved by Fritzing 0.9.3b)
breadboards: 1

parts:
  LCD1 = LCD screen
  부품1 = Arduino Uno (Rev3)
  hc-sr1 = hc-sr04
  hc-sr2 = hc-sr04

nets:
  GND: LCD1.VSS, LCD1.V0, LCD1.LED-, 부품1.GND, hc-sr1.GND, hc-sr2.GND
  VCC: LCD1.VDD, LCD1.LED+, 부품1.5V, hc-sr1.VCC, hc-sr2.VCC
  N1: LCD1.RS, 부품1.D12/MISO
  N2: LCD1.R/W, 부품1.D11_PWM/MOSI
  N3: LCD1.DB4, 부품1.D5_PWM
  N4: LCD1.DB5, 부품1.D4
  N5: LCD1.DB6, 부품1.D3_PWM
  N6: LCD1.DB7, 부품1.D2
  N7: 부품1.D9_PWM, hc-sr1.Echo
  N8: 부품1.D10_PWM/SS, hc-sr1.Trig
  N9: 부품1.D6_PWM, hc-sr2.Echo
  N10: 부품1.D7, hc-sr2.Trig
