# Fritzing sketch number5_2 (saved by Fritzing 0.9.3b)
breadboards: 1

parts:
  부품1 = Arduino Uno (Rev3) - ICSP
  LED1 = smd LED [color="Red (633nm)" package="0805 [SMD]"]
  S1 = Pushbutton [package="[THT]"]
  R1 = Resistor [tolerance=±5% resistance=220 package="2010 [SMD]"]

nets:
  N1: 부품1.D13/SCK, LED1.anode
  N2: 부품1.D2, S1.Pin_1, S1.Pin_2, R1.Pin_0
  N3: 부품1.5V, S1.Pin_3, S1.Pin_4
  N4: 부품1.GND, LED1.cathode, R1.Pin_1
